# Fritzing sketch ESP8266 Arduboy (saved by Fritzing 0.9.3b)
breadboards: 2

parts:
  WeMos_D1_Mini3 = WeMos D1 Mini  # not connected
  Piezo1 = Piezo Speaker - PC Mount [part_number=COM-07950]
  SW = IC, DIP package, 4 pins [chip_label=U]
  IC1 = DIP - 4 pins [chip_label=L package="DIP (Dual Inline) [THT]"]
  IC2 = DIP - 4 pins [chip_label=R package="DIP (Dual Inline) [THT]"]
  IC3 = DIP - 4 pins [chip_label=D package="DIP (Dual Inline) [THT]"]
  IC4 = DIP - 4 pins [chip_label=A package="DIP (Dual Inline) [THT]"]
  IC5 = DIP - 4 pins [chip_label=B package="DIP (Dual Inline) [THT]"]
  Squix1 = OLED 0.96" 128x64 I2C SSD1306 (GND/VCC)
  SW1 = IC, DIP package, 4 pins [chip_label=U]
  IC6 = DIP - 4 pins [chip_label=L package="DIP (Dual Inline) [THT]"]
  IC7 = DIP - 4 pins [chip_label=R package="DIP (Dual Inline) [THT]"]
  IC8 = DIP - 4 pins [chip_label=D package="DIP (Dual Inline) [THT]"]
  IC9 = DIP - 4 pins [chip_label=A package="DIP (Dual Inline) [THT]"]
  IC10 = DIP - 4 pins [chip_label=B package="DIP (Dual Inline) [THT]"]
  Piezo_Speaker = Piezo Speaker - PC Mount [part_number=COM-07950]
  I2C_OLED_SSD1306_128x64 = OLED 0.96" 128x64 I2C SSD1306 (GND/VCC)
  WeMos_D1_Mini4 = WeMos D1 Mini
  Volume_control = Trimmer Potentiometer [maximum_resistance=10kΩ package=THT]
  Paddle = Trimmer Potentiometer [maximum_resistance=10kΩ package=THT]

nets:
  GND: Piezo1.GND, SW.pin2, SW.pin3, Squix1.GND
  N1: SW.pin1, SW.pin4
  N2: IC1.pin2, IC2.pin2, IC3.pin2, IC3.pin3, IC4.pin1, IC4.pin4, IC5.pin1, IC5.pin4
  N3: IC3.pin1, IC3.pin4
  N4: IC4.pin2, IC4.pin3
  N5: IC5.pin2, IC5.pin3
  N6: SW1.pin2, IC8.pin3
  GND_2: SW1.pin3, IC6.pin3, Piezo_Speaker.GND, I2C_OLED_SSD1306_128x64.GND, WeMos_D1_Mini4.G, Volume_control.leg1, Paddle.leg1
  N7: SW1.pin4, WeMos_D1_Mini4.D5
  N8: IC6.pin1, WeMos_D1_Mini4.D6
  N9: IC7.pin1, IC8.pin2, IC9.pin2, IC10.pin2
  N10: IC7.pin2, WeMos_D1_Mini4.D7
  N11: IC8.pin1, WeMos_D1_Mini4.D4
  N12: IC9.pin4, WeMos_D1_Mini4.D3
  N13: IC10.pin4, WeMos_D1_Mini4.RX
  N14: Piezo_Speaker.VCC, Volume_control.wiper
  VCC: I2C_OLED_SSD1306_128x64.VCC, WeMos_D1_Mini4.3V3, Paddle.leg2
  N15: I2C_OLED_SSD1306_128x64.SCL, WeMos_D1_Mini4.D1
  N16: I2C_OLED_SSD1306_128x64.SCA, WeMos_D1_Mini4.D2
  N17: WeMos_D1_Mini4.A0, Paddle.wiper
  N18: WeMos_D1_Mini4.D8, Volume_control.leg2

notes:
  Expansion To I2C Sensors
  ESP8266 Arduboy
  cheungbx 2019-08-15

custom parts:
  Piezo Speaker - PC Mount: This is a small 12mm round speaker that operates around the audible 2kHz range. You can use these speakers to create simple music or user interfaces. Each speaker is PTH solderable and requires an operating voltage of 3.5-5V with a mean current of 35mA max. These speakers also have a typical sound output of 95 dBA and a coil resistance of 42 ±6.3 ohms.
  DIP - 4 pins: A DIP stand-in part for whatever IC you want. With 4 pins on a 300mil dual inline package (DIP) footprint.
  OLED 0.96" 128x64 I2C SSD1306 (GND/VCC): OLED 0.96" 128x64 I2C SSD1306 Pinout: GND/VCC/SCL/SDA
