# Fritzing sketch esp12e Arudboy (saved by Fritzing 0.9.3b)
circuit board: 8.46667cm x 5.64444cm

parts:
  ESP12E = ESP 12E
  SW2 = IC, DIP package, 4 pins [chip_label=U]
  IC11 = DIP - 4 pins [chip_label=L package="DIP (Dual Inline) [THT]"]
  IC12 = DIP - 4 pins [chip_label=R package="DIP (Dual Inline) [THT]"]
  IC13 = DIP - 4 pins [chip_label=D package="DIP (Dual Inline) [THT]"]
  IC14 = DIP - 4 pins [chip_label=A package="DIP (Dual Inline) [THT]"]
  IC15 = DIP - 4 pins [chip_label=B package="DIP (Dual Inline) [THT]"]
  Piezo_Speaker = Piezo Speaker - PC Mount [part_number=COM-07950]
  Squix3 = OLED 0.96" 128x64 I2C SSD1306 (GND/VCC)
  R1 = Resistor [tolerance=±5% resistance=10k package=THT]
  R = Resistor [tolerance=±5% resistance=10k package=THT]
  R4 = Resistor [tolerance=±5% resistance=10k package=THT]
  Volume_Control = Trimmer Potentiometer [maximum_resistance=10kΩ package=THT]

nets:
  N1: ESP12E.RX0, IC15.pin4
  N2: ESP12E.GPIO5, Squix3.SCL
  N3: ESP12E.GPIO4, Squix3.SCA
  N4: ESP12E.GPIO0, IC14.pin4, R4.Pin_1
  N5: ESP12E.GPIO2, IC13.pin1
  N6: ESP12E.GPIO15, Volume_Control.leg2
  GND: ESP12E.GND, Piezo_Speaker.GND, Volume_Control.leg1
  VCC: ESP12E.VCC, Squix3.VCC, R1.Pin_0, R4.Pin_0
  N7: ESP12E.GPIO13, IC12.pin3
  N8: ESP12E.GPIO12, IC11.pin4
  N9: ESP12E.GPIO14, SW2.pin4
  N10: ESP12E.EN, R1.Pin_1
  N11: ESP12E.RST, R.Pin_1
  N12: SW2.pin2, IC13.pin3
  N13: SW2.pin3, IC11.pin3, Squix3.GND
  N14: IC12.pin1, IC13.pin2, IC14.pin2, IC15.pin2
  N15: Piezo_Speaker.VCC, Volume_Control.wiper

notes:
  ESP8266_Arduboy
  cheungbx 2019-08-17
  pin layout for ESP12E
  All buttons tie to GND
  GPIO13 D7------ Right
  GPIO12 D6—— Left
  GPIO14 D5—— UP
  GPIO2 D4—— Down
  GPIO0 D3—— A
  GPIO3 RX —— B
  GPIO15 D8—— Speaker
  GPIO 15 D8-[ 10k ]--- GND
  Reset ——[ 10k ]----VCC
  EN ——[ 10k ]----VCC
  GPIO 0 D3-- [ 10k ]--- VCC
  Exp USB_ESP01
  Port Programmer
  1 VCC 3.3V
  2 GND GND
  3 GPIO5 D1 (SCL) N.C.
  4 GPIO4 D2 (SDA) N.C.
  5 LIPO Charge 5V
  6 TX GPIO1 D10 TX0
  7 RX GPIO3 D9 RX
  8 GPIO0 D3 IO0
  9 Reset Reset
  10 A0 NC

custom parts:
  ESP 12E: ESP 12e module with spi interface and wifi connection
  DIP - 4 pins: A DIP stand-in part for whatever IC you want. With 4 pins on a 300mil dual inline package (DIP) footprint.
  Piezo Speaker - PC Mount: This is a small 12mm round speaker that operates around the audible 2kHz range. You can use these speakers to create simple music or user interfaces. Each speaker is PTH solderable and requires an operating voltage of 3.5-5V with a mean current of 35mA max. These speakers also have a typical sound output of 95 dBA and a coil resistance of 42 ±6.3 ohms.
  OLED 0.96" 128x64 I2C SSD1306 (GND/VCC): OLED 0.96" 128x64 I2C SSD1306 Pinout: GND/VCC/SCL/SDA
